// Logisim project Universal_shift_reg.circ as structural Verilog
module Universal_Shift_Register (
  input  I1,
  input  I0,
  input  I2,
  input  I3,
  input  D1,
  input  D0,
  input  [1:0] Selector,
  input  Preset,
  input  Reset
);

  wire clock_1_out, d_ff_1_q, d_ff_2_q, d_ff_3_q, d_ff_4_q, multiplexer_1_out, multiplexer_2_out,
       multiplexer_3_out, multiplexer_4_out;

  Clock clock_1 (.out(clock_1_out));
  Multiplexer #(.select(2)) multiplexer_1 (
    .in0(D0), .in1(d_ff_2_q), .in2(I0), .in3(d_ff_1_q), .out(multiplexer_1_out), .sel(Selector));
  D_Flip_Flop d_ff_1 (
    .D(multiplexer_1_out), .clk(clock_1_out), .Q(d_ff_1_q), .preset(Preset), .reset(Reset));  // open: Qn
  Multiplexer #(.select(2)) multiplexer_2 (
    .in0(d_ff_1_q), .in1(d_ff_3_q), .in2(I1), .in3(d_ff_2_q), .out(multiplexer_2_out), .sel(Selector));
  D_Flip_Flop d_ff_2 (
    .D(multiplexer_2_out), .clk(clock_1_out), .Q(d_ff_2_q), .preset(Preset), .reset(Reset));  // open: Qn
  Multiplexer #(.select(2)) multiplexer_3 (
    .in0(d_ff_2_q), .in1(d_ff_4_q), .in2(I2), .in3(d_ff_3_q), .out(multiplexer_3_out), .sel(Selector));
  D_Flip_Flop d_ff_3 (
    .D(multiplexer_3_out), .clk(clock_1_out), .Q(d_ff_3_q), .preset(Preset), .reset(Reset));  // open: Qn
  Multiplexer #(.select(2)) multiplexer_4 (
    .in0(d_ff_3_q), .in1(D1), .in2(I3), .in3(d_ff_4_q), .out(multiplexer_4_out), .sel(Selector));
  D_Flip_Flop d_ff_4 (
    .D(multiplexer_4_out), .clk(clock_1_out), .Q(d_ff_4_q), .preset(Preset), .reset(Reset));  // open: Qn
endmodule
