// Logisim project carry_forward_adder.circ as structural Verilog: 1 circuit, main circuit main
module main (
  input  x0,
  input  y0,
  input  co,
  input  x1,
  input  y1,
  input  x2,
  input  y2,
  input  x3,
  input  y3,
  input  in_10,
  output s0,
  output c1,
  output s1,
  output c2,
  output s2,
  output c3,
  output s3,
  output c4
);

  wire and_1_out, g0_out, g1_out, g2_out, g3_out, p0_out, p1_out, p1g0_out, p1p0c0_out, p2_out, p2g1_out,
       p2p1g0_out, p2p1p0c0_out, p3_out, p3g2_out, p3p2g1_out, p3p2p1g0_out, p3p2p1p0c0_out;

  xor p0 (p0_out, x0, y0);
  and g0 (g0_out, y0, x0);
  xor p1 (p1_out, x1, y1);
  and g1 (g1_out, y1, x1);
  xor p2 (p2_out, x2, y2);
  xor p3 (p3_out, x3, y3);
  and g2 (g2_out, y2, x2);
  xor xor_1 (s0, p0_out, co);
  and g3 (g3_out, x3, y3);
  and and_1 (and_1_out, p0_out, co);
  xor xor_2 (s1, p1_out, c1);
  and p1g0 (p1g0_out, g0_out, p1_out);
  and p3g2 (p3g2_out, p3_out, g2_out);
  xor xor_3 (s2, p2_out, c2);
  and p2g1 (p2g1_out, g1_out, p2_out);
  xor xor_4 (s3, p3_out, c3);
  or or_1 (c1, and_1_out, g0_out);
  and p1p0c0 (p1p0c0_out, co, p1_out, p0_out);
  and p3p2g1 (p3p2g1_out, p3_out, p2_out, g1_out);
  and p3p2p1g0 (p3p2p1g0_out, p3_out, p2_out, p1_out, g0_out);
  and p2p1g0 (p2p1g0_out, g0_out, p1_out, p2_out);
  and p2p1p0c0 (p2p1p0c0_out, p2_out, p1_out, p0_out, co);
  or or_2 (c2, g1_out, p1g0_out, p1p0c0_out);
  and p3p2p1p0c0 (p3p2p1p0c0_out, p3_out, p2_out, p0_out, p1_out, co);
  or or_3 (c3, g2_out, p2g1_out, p2p1g0_out, p2p1p0c0_out);
  or or_4 (c4, g3_out, p3g2_out, p3p2g1_out, p3p2p1g0_out, p3p2p1p0c0_out);
  Hex_Digit_Display hex_digit_display_1 (.value({s3, s2, s1, s0}));  // open: dp
  Hex_Digit_Display hex_digit_display_2 (.value({{3{in_10}}, c4}));  // open: dp
endmodule
